// Logisim project cache.circ as structural Verilog: 2 circuits, main circuit main
module main (
  input  [31:0] Address,
  input  [31:0] Data_in,
  output [31:0] Data_Out
);
endmodule

module line (
  input  Clock,
  input  [31:0] Address,
  input  [7:0] Data_In,
  input  [1:0] in_4,
  output Hit,
  output [7:0] Data_Out
);

  wire comparator_1_eq, s_r_ff_1_q, undriven;
  wire [21:0] Tag_q;

  S_R_Flip_Flop s_r_ff_1 (.S(undriven), .clk(Clock), .Q(s_r_ff_1_q));  // open: R, Qn, preset, reset, en
  Register #(.width(22)) Tag (.D(Address[31:10]), .en(undriven), .Q(Tag_q), .clk(Clock));  // open: clr
  and and_1 (Hit, s_r_ff_1_q, comparator_1_eq);
  Comparator #(.width(22)) comparator_1 (.a(Tag_q), .b(Address[31:10]), .eq(comparator_1_eq));  // open: gt, lt
  RAM #(.addrWidth(10), .bus("separate")) ram_1 (
    .addr(Address[9:0]), .din(Data_In), .data(Data_Out), .clk(Clock));  // open: str, sel, ld, clr
endmodule
